# Fritzing sketch schematic (saved by Fritzing 0.9.3b)
breadboards: 1

parts:
  Onderdeel1 = Intel Galileo
  U1 = L298 [package=multiwatt15]
  U2 = LCD-16X2 [package=lcd-16x2_noholes]
  LCM1602_IIC2 = LCM1602 IIC [part_number="LCM1602 IIC" chip_label="LCM1602 IIC" package="DIP (Dual Inline) [THT]"]
  M3 = DC Motor
  M4 = DC Motor
  S1 = Pushbutton [package="[THT]"]
  R1 = Resistor [tolerance=±5% resistance=220 package="2512 [SMD]"]
  LED1 = LED - 3mm [color="Red (633nm)" package="3 mm [THT]"]
  LED2 = LED - 3mm [color="Red (633nm)" package="3 mm [THT]"]
  hc-sr1 = hc-sr04
  R2 = Resistor [tolerance=±5% resistance=220 package="2512 [SMD]"]
  R3 = Resistor [tolerance=±5% resistance=220 package="2512 [SMD]"]

nets:
  N1: Onderdeel1.D12/MISO, LED2.anode
  N2: Onderdeel1.D13/SCK, LED1.anode
  N3: Onderdeel1.A4/SDA, LCM1602_IIC2.SDA
  N4: Onderdeel1.A5/SCL, LCM1602_IIC2.SCL
  N5: Onderdeel1.D2, R1.Pin_0
  N6: Onderdeel1.D3_PWM, hc-sr1.Echo
  N7: Onderdeel1.D4, hc-sr1.Trig
  VCC: Onderdeel1.5V, U1.VS, LCM1602_IIC2.VCC, S1.Pin_1, S1.Pin_2, S1.Pin_3, S1.Pin_4, R1.Pin_1, hc-sr1.VCC, R2.Pin_1, R3.Pin_1
  GND: Onderdeel1.GND, U1.CSA, U1.GND, U1.VLS, U1.CSB, LCM1602_IIC2.GND, LED1.cathode, LED2.cathode, hc-sr1.GND
  N8: U1.OUT1, M4.pin_1
  N9: U1.OUT2, M4.pin_2
  N10: U1.ENA, R3.Pin_0
  N11: U1.ENB, R2.Pin_0
  N12: U1.OUT3, M3.pin_2
  N13: U1.OUT4, M3.pin_1
  VSS: U2.VSS, LCM1602_IIC2.VSS
  VDD: U2.VDD, LCM1602_IIC2.VDD
  N14: U2.VO, LCM1602_IIC2.V0
  N15: U2.RS, LCM1602_IIC2.RS
  N16: U2.R_W, LCM1602_IIC2.RW
  N17: U2.E, LCM1602_IIC2.E
  N18: U2.DB0, LCM1602_IIC2.D0
  N19: U2.DB1, LCM1602_IIC2.D1
  N20: U2.DB2, LCM1602_IIC2.D2
  N21: U2.DB3, LCM1602_IIC2.D3
  N22: U2.DB4, LCM1602_IIC2.D4
  N23: U2.DB5, LCM1602_IIC2.D5
  N24: U2.DB6, LCM1602_IIC2.D6
  N25: U2.DB7, LCM1602_IIC2.D7
  N26: U2.A, LCM1602_IIC2.A
  N27: U2.K, LCM1602_IIC2.K
  N28: LCM1602_IIC2.LED_A, LCM1602_IIC2.LED_B

notes:
  1-8
  15 - 9
  Enable A & B op HIGH
  pin 2 & 3:
  galileo interrupts
  Input 4-1
  board:
  pin 3 is echo
  pin 4 is trigger

custom parts:
  LCM1602 IIC: I2C-Module to use a 1602 or 2004 LCD on with the wire.h libory Serial LCD Modul
